# Fritzing sketch esp32-sd-card-and-tft-display (saved by Fritzing 1.0.1rc)
breadboards: 1

parts:
  Part1 = node32s
  sdCard1 = my_sdCard  # not connected
  Part2 = TFT 2.2 inch 320x240 w microSD [part_number=1480]

nets:
  3.3V: Part1.3.3V, Part2.VIN, Part2.BACKLIGHT
  N1: Part1.V_BATT, Part2.GND
  N2: Part1.IO23, Part2.MOSI
  N3: Part1.IO19, Part2.MISO
  N4: Part1.IO18, Part2.SCLK

notes:
  Instead of VBATT is GND on my board

custom parts:
  my_sdCard: micro sdCard Adapter with 90º pin header. Use a filtering Capacitor between CS and GND if needed. PCB View Pinouts are Reversed for laying parallel on PCB using a 90º pin header.
  TFT 2.2 inch 320x240 w microSD: This lovely little display breakout is the best way to add a small, colorful and bright display to any project. Since the display uses 4-wire SPI to communicate and has its own pixel-addressable frame buffer, it can be used with every kind of microcontroller. Even a very small one with low memory and few pins available! The 2.2" display has 320x240 color pixels.
